# Fritzing sketch IoT_circuit (saved by Fritzing 0.9.3b)

parts:
  Load_Cell1 = Load Cell - Red/white/black/green
  Part1 = HX711 Weighing Sensor Module
  Adafruit_HUZZAH_ESP8266_Breakout1 = Adafruit HUZZAH ESP8266 Breakout [part_number=2471]
  BAT1 = BC9VPC [package=bc9vpc]
  U3 = Voltage Regulator - 3.3V [package="TO220 [THT]"]
  U4 = TEMPERATURE-SENSOR [package=to-92]

nets:
  N1: Load_Cell1.wire1, Part1.E+
  N2: Load_Cell1.wire2, Part1.A+
  N3: Load_Cell1.wire3, Part1.E-
  N4: Load_Cell1.wire4, Part1.A-
  VCC: Part1.VCC, Adafruit_HUZZAH_ESP8266_Breakout1.3V, U4.VCC
  GND: Part1.GND, Adafruit_HUZZAH_ESP8266_Breakout1.GND, U4.GND
  N5: Part1.DO/RX, Adafruit_HUZZAH_ESP8266_Breakout1.#2
  N6: Part1.CK/TX, Adafruit_HUZZAH_ESP8266_Breakout1.#0
  N7: Adafruit_HUZZAH_ESP8266_Breakout1.#4, U4.ADJ
  N8: Adafruit_HUZZAH_ESP8266_Breakout1.V+, U3.output_voltage
  N9: BAT1.V+, U3.input_voltage
  N10: BAT1.V-, U3.GND

custom parts:
  Load Cell - Red/white/black/green: A rectangle load cell/weighting pressure Sensor with four wires - Red, white, black, green. Normally corresponding with E+, E-, A+, A- respectively.
  HX711 Weighing Sensor Module: HX711 is a precision 24-bit analog-to-digital converter (ADC) designed for weigh scales and industrial control applications to interface directly with a bridge sensor.
